# Fritzing sketch ultracounter (saved by Fritzing 0.9.3b)
breadboards: 1

parts:
  Part1 = Arduino Uno (Rev3)
  hc-sr1 = hc-sr04
  hc-sr2 = hc-sr04

nets:
  N1: Part1.D9_PWM, hc-sr2.Echo
  N2: Part1.D10_PWM/SS, hc-sr2.Trig
  N3: Part1.D12/MISO, hc-sr1.Echo
  N4: Part1.D13/SCK, hc-sr1.Trig
  VCC: Part1.5V, hc-sr1.VCC, hc-sr2.VCC
  GND: Part1.GND, hc-sr1.GND, hc-sr2.GND

// code stored in the sketch: ultracounter.ino
#define trigPin 13
#define echoPin 12
int counter = 0;
int currentState = 0;
int previousState = 0;
void setup() {
 Serial.begin (9600);
 pinMode(trigPin, OUTPUT);
 pinMode(echoPin, INPUT);
}

void loop() {
 long duration, distance;
 digitalWrite(trigPin, LOW); 
 delayMicroseconds(2); 
 digitalWrite(trigPin, HIGH);
 delayMicroseconds(10); 
 digitalWrite(trigPin, LOW);
 duration = pulseIn(echoPin, HIGH);
 distance = (duration/2) / 29.1;
 if (distance <= 10){
 currentState = 1;
 }
 else {
 currentState = 0;
 }
 delay(100);
 if(currentState != previousState){
if(currentState == 1){
counter = counter + 1;
Serial.println(counter);
}
}
}
